# Fritzing sketch Energy Tracker using arduio ESP (saved by Fritzing 1.0.2b)
circuit board: 9.94125cm x 4.80457cm
breadboards: 1

parts:
  C3 = Electrolytic Capacitor [capacitance=1μF voltage=35V package="0405 [SMD, electrolytic]"]
  Part2 = Adafruit 1.44 inch TFT Breakout [part_number="Adafruit #2088"]
  R12 = Resistor [tolerance=±5% resistance=1k package="1206 [SMD]"]
  R11 = Resistor [tolerance=±5% resistance=33 package="1206 [SMD]"]
  R9 = Resistor [tolerance=±5% resistance=10k package="1206 [SMD]"]
  R10 = Resistor [tolerance=±5% resistance=10k package="1206 [SMD]"]
  TRS1 = Audio Jack (TRS) 3.5mm [package="PG203J [THT]"]
  Part3 = Barduino4.0

nets:
  N1: C3.-, Part2.GND, R9.Pin_0, Part3.GND#29
  N2: C3.+, R11.Pin_0, R9.Pin_1, R10.Pin_1, TRS1.Sleeve
  N3: Part2.VIN, R10.Pin_0, Part3.3V3#30
  N4: Part2.SCK, Part3.USB
  N5: Part2.MOSI, Part3.11
  N6: Part2.TFTCS, Part3.10
  N7: Part2.RESET, Part3.09
  N8: Part2.TFTDC, Part3.08
  N9: R12.Pin_0, Part3.01
  N10: R12.Pin_1, R11.Pin_1, TRS1.Ring, TRS1.Tip
  N11: Part3.02#18, Part3.GND#33
  N12: Part3.04, Part3.3V3#32
  N13: Part3.02#61, Part3.3V3#62

custom parts:
  Adafruit 1.44 inch TFT Breakout: This lovely little display breakout is the best way to add a small, colorful and bright display to any project. Since the display uses 4-wire SPI to communicate and has its own pixel-addressable frame buffer, it can be used with every kind of microcontroller. Even a very small one with low memory and few pins available! The 1.44" display has 128x128 color pixels. Unlike the low cost "Nokia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
